// Logisim project bcd_adder.circ as structural Verilog: 3 circuits, main circuit main
module main (
  input  [3:0] A100,
  input  [3:0] B100,
  input  [3:0] A10,
  input  [3:0] B10,
  input  Cin,
  input  [3:0] A1,
  input  [3:0] B1,
  output [3:0] S100,
  output Cout,
  output [3:0] S10,
  output [3:0] S1
);

  wire C1_1, C1_10, C1_100, CORR_1, CORR_10, GT_1, GT_10, GT_100;
  wire [3:0] and_1_out, and_2_out, and_3_out, bit_extender_1_out, bit_extender_2_out, bit_extender_3_out,
       Z_1, Z_10, Z_100;

  Adder #(.width(4)) adder_1 (.a(A100), .b(B100), .out(Z_100), .cin(CORR_10), .cout(C1_100));
  Adder #(.width(4)) adder_2 (.a(A1), .b(B1), .out(Z_1), .cin(Cin), .cout(C1_1));
  Adder #(.width(4)) adder_3 (.a(A10), .b(B10), .out(Z_10), .cin(CORR_1), .cout(C1_10));
  Comparator #(.mode("unsigned"), .width(4)) comparator_1 (.a(Z_100), .b(4'b1001), .gt(GT_100));  // open: eq, lt
  Comparator #(.mode("unsigned"), .width(4)) comparator_2 (.a(Z_1), .b(4'b1001), .gt(GT_1));  // open: eq, lt
  assign bit_extender_1_out = {{3{Cout}}, Cout};  // Bit_Extender bit_extender_1
  or or_1 (Cout, C1_100, GT_100);
  Comparator #(.mode("unsigned"), .width(4)) comparator_3 (.a(Z_10), .b(4'b1001), .gt(GT_10));  // open: eq, lt
  assign bit_extender_2_out = {{3{CORR_10}}, CORR_10};  // Bit_Extender bit_extender_2
  or or_2 (CORR_10, C1_10, GT_10);
  assign bit_extender_3_out = {{3{CORR_1}}, CORR_1};  // Bit_Extender bit_extender_3
  or or_3 (CORR_1, C1_1, GT_1);
  assign and_1_out = 4'b0110 & bit_extender_1_out;  // AND_Gate and_1, 4 bits wide
  Adder #(.width(4)) adder_4 (.a(Z_100), .b(and_1_out), .out(S100), .cin(1'b0));  // open: cout
  assign and_2_out = 4'b0110 & bit_extender_2_out;  // AND_Gate and_2, 4 bits wide
  assign and_3_out = 4'b0110 & bit_extender_3_out;  // AND_Gate and_3, 4 bits wide
  Adder #(.width(4)) adder_5 (.a(Z_10), .b(and_2_out), .out(S10), .cin(1'b0));  // open: cout
  Adder #(.width(4)) adder_6 (.a(Z_1), .b(and_3_out), .out(S1), .cin(1'b0));  // open: cout
  Hex_Digit_Display hex_digit_display_1 (.value(S100));  // open: dp
  Hex_Digit_Display hex_digit_display_2 (.value(S10));  // open: dp
  Hex_Digit_Display hex_digit_display_3 (.value(S1));  // open: dp
  LED led_1 (.in(Cout));

  // Other names for the same wires on the sheet: CORR_100 = Cout; Cout1 = CORR_1; Cout10 = CORR_10
endmodule

module full_adder (
  input  A,
  input  B,
  input  Cin,
  output Sum,
  output Cout
);

  wire P1, P2, X1;

  xor xor_1 (X1, A, B);
  and and_1 (P1, A, B);
  xor xor_2 (Sum, X1, Cin);
  and and_2 (P2, X1, Cin);
  or or_1 (Cout, P1, P2);
endmodule

module bcd_digit (
  input  Cin,
  input  [3:0] A,
  input  [3:0] B,
  output [3:0] S,
  output Cout
);

  wire C1, GT;
  wire [3:0] and_1_out, bit_extender_1_out, Z;

  Adder #(.width(4)) adder_1 (.a(A), .b(B), .out(Z), .cin(Cin), .cout(C1));
  Comparator #(.mode("unsigned"), .width(4)) comparator_1 (.a(Z), .b(4'b1001), .gt(GT));  // open: eq, lt
  assign bit_extender_1_out = {{3{Cout}}, Cout};  // Bit_Extender bit_extender_1
  or or_1 (Cout, C1, GT);
  assign and_1_out = 4'b0110 & bit_extender_1_out;  // AND_Gate and_1, 4 bits wide
  Adder #(.width(4)) adder_2 (.a(Z), .b(and_1_out), .out(S), .cin(1'b0));  // open: cout
  Hex_Digit_Display hex_digit_display_1 (.value(S));  // open: dp

  // Other names for the same wires on the sheet: CORR = Cout
endmodule
