// Logisim project carry_select_adder.circ as structural Verilog: 3 circuits, main circuit main
module main (
  input  [5:0] A,
  input  [5:0] B,
  input  Cin,
  output [5:0] S,
  output Cout
);

  wire C1, C3, C3_0, C3_1, C3_a, C3_b, C5_0, C5_1, COUTFINAL_a, COUTFINAL_b, NC1, NC3, S2_0, S2_1, S2_sel_a,
       S2_sel_b, S3_0, S3_1, S3_sel_a, S3_sel_b, S4_0, S4_1, S4_sel_a, S4_sel_b, S5_0, S5_1, S5_sel_a,
       S5_sel_b;

  adder2 AD0 (.A(A[1:0]), .B(B[1:0]), .Cin(Cin), .S(S[1:0]), .Cout(C1));
  adder2 AD1_0 (.A(A[3:2]), .B(B[3:2]), .Cin(1'b0), .S({S3_0, S2_0}), .Cout(C3_0));
  adder2 AD1_1 (.A(A[3:2]), .B(B[3:2]), .Cin(1'b1), .S({S3_1, S2_1}), .Cout(C3_1));
  adder2 AD2_0 (.A(A[5:4]), .B(B[5:4]), .Cin(1'b0), .S({S5_0, S4_0}), .Cout(C5_0));
  adder2 AD2_1 (.A(A[5:4]), .B(B[5:4]), .Cin(1'b1), .S({S5_1, S4_1}), .Cout(C5_1));
  // XOR_Gate xor_1 has open pins: out=NC1
  and and_1 (S2_sel_a, C1, S2_1);
  and and_2 (S2_sel_b, NC1, S2_0);
  and and_3 (S3_sel_a, C1, S3_1);
  and and_4 (S3_sel_b, NC1, S3_0);
  and and_5 (C3_a, C1, C3_1);
  and and_6 (C3_b, NC1, C3_0);
  // XOR_Gate xor_2 has open pins: out=NC3
  and and_7 (S4_sel_a, C3, S4_1);
  and and_8 (S4_sel_b, NC3, S4_0);
  and and_9 (S5_sel_a, C3, S5_1);
  and and_10 (S5_sel_b, NC3, S5_0);
  and and_11 (COUTFINAL_a, C3, C5_1);
  and and_12 (COUTFINAL_b, NC3, C5_0);
  or or_1 (S[2], S2_sel_a, S2_sel_b);
  or or_2 (S[3], S3_sel_a, S3_sel_b);
  or or_3 (C3, C3_a, C3_b);
  or or_4 (S[4], S4_sel_a, S4_sel_b);
  or or_5 (S[5], S5_sel_a, S5_sel_b);
  or or_6 (Cout, COUTFINAL_a, COUTFINAL_b);

  // Other names for the same wires on the sheet: CINREAL = Cin; COUTFINAL = Cout; GA0[1:0] = A[1:0];
  //   GA1[1:0] = A[3:2]; GA2[1:0] = A[5:4]; GB0[1:0] = B[1:0]; GB1[1:0] = B[3:2]; GB2[1:0] = B[5:4]; S6OUT[5:0] = S;
  //   SG0[1:0] = S[1:0]; S2_sel = S[2]; S3_sel = S[3]; S4_sel = S[4]; S5_sel = S[5]; SG1_0[1:0] = {S3_0, S2_0};
  //   SG1_1[1:0] = {S3_1, S2_1}; SG2_0[1:0] = {S5_0, S4_0}; SG2_1[1:0] = {S5_1, S4_1}
endmodule

module full_adder (
  input  A,
  input  B,
  input  Cin,
  output Sum,
  output Cout
);

  wire P1, P2, X1;

  xor xor_1 (X1, A, B);
  and and_1 (P1, A, B);
  xor xor_2 (Sum, X1, Cin);
  and and_2 (P2, X1, Cin);
  or or_1 (Cout, P1, P2);
endmodule

module adder2 (
  input  Cin,
  input  [1:0] A,
  input  [1:0] B,
  output [1:0] S,
  output Cout
);

  wire C1;

  full_adder FA1 (.A(A[1]), .B(B[1]), .Cin(C1), .Sum(S[1]), .Cout(Cout));
  full_adder FA0 (.A(A[0]), .B(B[0]), .Cin(Cin), .Sum(S[0]), .Cout(C1));

  // Other names for the same wires on the sheet: A2[1:0] = A; B2[1:0] = B; COUTF = Cout; S2OUT[1:0] = S
endmodule
