// Logisim project multiplier.circ as structural Verilog: 2 circuits, main circuit main
module multiplier (
  input  [3:0] A,
  input  [3:0] B,
  input  start,
  input  clk,
  output [7:0] C,
  output \end 
);

  wire CO, GND, M0, M1, M2, M3, nST, RUN, S0, S1, S2, S3, VCC;

  _7408 U1 (
    .pin1(A[0]), .pin2(C[0]), .pin3(M0), .pin4(A[1]), .pin5(C[0]), .pin6(M1), .pin13(C[0]), .pin12(A[3]),
    .pin11(M3), .pin10(C[0]), .pin9(A[2]), .pin8(M2));
  _7404 U6 (
    .pin1(start), .pin2(nST), .pin3(\end ), .pin4(RUN), .pin5(GND), .pin13(GND), .pin11(GND), .pin9(GND));  // open: pin6, pin12, pin10, pin8
  _74283 U2 (
    .pin1(S1), .pin2(M1), .pin3(C[5]), .pin4(S0), .pin5(C[4]), .pin6(M0), .pin7(GND), .pin15(M2),
    .pin14(C[6]), .pin13(S2), .pin12(C[7]), .pin11(M3), .pin10(S3), .pin9(CO));
  _74161 U5 (
    .pin1(nST), .pin2(clk), .pin3(GND), .pin4(GND), .pin5(GND), .pin6(GND), .pin7(RUN), .pin12(\end ),
    .pin10(RUN), .pin9(VCC));  // open: pin15, pin14, pin13, pin11
  _74194 U3 (
    .pin1(nST), .pin2(GND), .pin3(CO), .pin4(S3), .pin5(S2), .pin6(S1), .pin7(GND), .pin15(C[7]),
    .pin14(C[6]), .pin13(C[5]), .pin12(C[4]), .pin11(clk), .pin10(RUN), .pin9(RUN));
  _74194 U4 (
    .pin1(VCC), .pin2(S0), .pin3(B[3]), .pin4(B[2]), .pin5(B[1]), .pin6(B[0]), .pin7(GND), .pin15(C[3]),
    .pin14(C[2]), .pin13(C[1]), .pin12(C[0]), .pin11(clk), .pin10(start), .pin9(RUN));
  // also tied to GND on the sheet: GND
  // also tied to VCC on the sheet: VCC

  // Other names for the same wires on the sheet: Q0 = C[0]; Q1 = C[1]; Q2 = C[2]; Q3 = C[3]; AC0 = C[4]; AC1 = C[5];
  //   AC2 = C[6]; AC3 = C[7]; ST = start

  // Notes on the sheet:
  //   INPUTS
  //   U1  7408  AND: M = A . Q0
  //   U6  7404  inverters
  //   U2  74283  ADDER: ACC + M
  //   U5  74161  cycle counter
  //   U3  74194  ACC register
  //   U4  74194  Q register
  //   OUTPUTS
endmodule

module main (
  input  [3:0] A,
  input  [3:0] B,
  input  start,
  output [7:0] C,
  output \end 
);

  wire CLK_out;

  Clock CLK (.out(CLK_out));
  multiplier multiplier_1 (.A(A), .B(B), .start(start), .clk(CLK_out), .C(C), .\end (\end ));

  // Notes on the sheet:
  //   4-bit x 4-bit shift-and-add multiplier  (74-series TTL)
  //   start = 1, one clock tick to load, then start = 0 and 4 ticks -> end = 1
endmodule
