// Logisim project arc_4.circ as structural Verilog: 1 circuit, main circuit main
module main (
  input  [31:0] A,
  input  [31:0] B,
  input  Operator,
  input  start,
  output [31:0] C,
  output Overflow,
  output [7:0] out_7,
  output \end 
);

  wire A_smaller, and_1_out, and_2_out, and_4_out, buffer_1_out, c_out, comparator_2_eq, comparator_4_eq,
       comparator_4_gt, EA_smaller, Es_equal, has_c_out, M2_zero, MA_smaller, not_1_out, not_2_out,
       not_3_out, Op, overflow_t, S, xor_1_out;
  wire [0:0] MAoMB;
  wire [4:0] L, multiplexer_9_out, priority_encoder_1_out;
  wire [7:0] adder_1_out, E, multiplexer_1_out, multiplexer_5_out, subtractor_1_out, subtractor_2_out,
       subtractor_3_out;
  wire [22:0] M, M1, M2;
  wire [23:0] adder_2_out, MA_chosen, MA_shifted, MB_chosen, MB_shifted, multiplexer_7_out, subtractor_4_out,
       subtractor_5_out;
  wire [23:23] shifter_3_out;

  and and_1 (and_1_out, A_smaller, Op);
  and and_2 (and_2_out, Es_equal, MA_smaller);
  xor xor_1 (xor_1_out, Operator, A[31]);
  xor xor_2 (S, and_1_out, A[31]);
  xor xor_3 (Op, xor_1_out, B[31]);
  Subtractor subtractor_1 (.a(A[30:23]), .b(B[30:23]), .out(subtractor_1_out));  // open: bin, bout
  Subtractor subtractor_2 (.a(B[30:23]), .b(A[30:23]), .out(subtractor_2_out));  // open: bin, bout
  or or_1 (A_smaller, EA_smaller, and_2_out);
  Comparator #(.mode("unsigned")) comparator_1 (
    .a(A[30:23]), .b(B[30:23]), .eq(Es_equal), .lt(EA_smaller));  // open: gt
  Multiplexer #(.width(8)) multiplexer_1 (
    .in0(subtractor_1_out), .in1(subtractor_2_out), .out(multiplexer_1_out), .sel(EA_smaller));
  Shifter #(.shift("lr"), .width(24)) shifter_1 (
    .in({1'b1, B[22:0]}), .\dist (multiplexer_1_out[4:0]), .out(MB_shifted));
  Shifter #(.shift("lr"), .width(24)) shifter_2 (
    .in({1'b1, A[22:0]}), .\dist (multiplexer_1_out[4:0]), .out(MA_shifted));
  Multiplexer #(.width(8)) multiplexer_2 (.in0(A[30:23]), .in1(B[30:23]), .out(out_7), .sel(EA_smaller));
  Adder adder_1 (.a(out_7), .b(8'h1), .out(adder_1_out));  // open: cin, cout
  Subtractor subtractor_3 (.a(out_7), .b({3'b000, L}), .out(subtractor_3_out));  // open: bin, bout
  Multiplexer #(.width(24)) multiplexer_3 (.in0({1'b1, A[22:0]}), .in1(MA_shifted), .out(MA_chosen), .sel(EA_smaller));
  Multiplexer #(.width(24)) multiplexer_4 (.in0({1'b1, B[22:0]}), .in1(MB_shifted), .out(MB_chosen), .sel(not_1_out));
  not not_1 (not_1_out, EA_smaller);
  Multiplexer #(.width(8)) multiplexer_5 (
    .in0(subtractor_3_out), .in1({8{1'b0}}), .out(multiplexer_5_out), .sel(comparator_2_eq));
  Comparator #(.width(23)) comparator_2 (.a(M1), .b({23{1'b0}}), .eq(comparator_2_eq));  // open: gt, lt
  Multiplexer #(.width(8)) multiplexer_6 (.in0(adder_1_out), .in1(multiplexer_5_out), .out(E), .sel(not_2_out));
  not not_2 (not_2_out, has_c_out);
  Subtractor #(.width(24)) subtractor_4 (.a(MA_chosen), .b(MB_chosen), .out(subtractor_4_out));  // open: bin, bout
  Subtractor #(.width(24)) subtractor_5 (.a(MB_chosen), .b(MA_chosen), .out(subtractor_5_out));  // open: bin, bout
  Comparator #(.mode("unsigned"), .width(24)) comparator_3 (
    .a(MA_chosen), .b(MB_chosen), .lt(MA_smaller));  // open: gt, eq
  not not_3 (not_3_out, Op);
  Adder #(.width(24)) adder_2 (.a(MA_chosen), .b(MB_chosen), .out(adder_2_out), .cout(c_out));  // open: cin
  Multiplexer #(.width(24)) multiplexer_7 (
    .in0(subtractor_4_out), .in1(subtractor_5_out), .out(multiplexer_7_out), .sel(MA_smaller));
  Comparator #(.mode("unsigned")) comparator_4 (
    .a(out_7), .b(8'hfe), .gt(comparator_4_gt), .eq(comparator_4_eq));  // open: lt
  Multiplexer #(.width(24)) multiplexer_8 (.in0(adder_2_out), .in1(multiplexer_7_out), .out({M1, MAoMB[0]}), .sel(Op));
  and and_3 (has_c_out, c_out, not_3_out);
  and and_4 (and_4_out, comparator_4_eq, has_c_out);
  or or_2 (overflow_t, comparator_4_gt, and_4_out);
  Priority_Encoder #(.select(5)) priority_encoder_1 (
    .in0(MAoMB[0]), .in1(M1[0]), .in2(M1[1]), .in3(M1[2]), .in4(M1[3]), .in5(M1[4]), .in6(M1[5]),
    .in7(M1[6]), .in8(M1[7]), .in9(M1[8]), .in10(M1[9]), .in11(M1[10]), .in12(M1[11]), .in13(M1[12]),
    .in14(M1[13]), .in15(M1[14]), .in16(M1[15]), .in17(M1[16]), .in18(M1[17]), .in19(M1[18]), .in20(M1[19]),
    .in21(M1[20]), .in22(M1[21]), .in23(M1[22]), .in24(1'b0), .in25(1'b0), .in26(1'b0), .in27(1'b0),
    .in28(1'b0), .in29(1'b0), .in30(1'b0), .in31(1'b0), .out(priority_encoder_1_out), .en_out(M2_zero));  // open: gs, en_in
  Multiplexer #(.width(5)) multiplexer_9 (
    .in0(priority_encoder_1_out), .in1(5'b10111), .out(multiplexer_9_out), .sel(M2_zero));
  Subtractor #(.width(5)) subtractor_6 (.a(5'b10111), .b(multiplexer_9_out), .out(L));  // open: bin, bout
  Shifter #(.width(24)) shifter_3 (.in({M1, MAoMB[0]}), .\dist (L), .out({shifter_3_out[23], M2}));
  Multiplexer #(.width(23)) multiplexer_10 (.in0(M2), .in1(M1), .out(M), .sel(has_c_out));
  buf buffer_1 (buffer_1_out, start);
  Register #(.width(1)) register_1 (.D(S), .clk(buffer_1_out), .Q(C[31]));  // open: en, clr
  Register register_2 (.D(E), .clk(buffer_1_out), .Q(C[30:23]));  // open: en, clr
  Register #(.width(23)) register_3 (.D(M), .clk(buffer_1_out), .Q(C[22:0]));  // open: en, clr
  Register #(.width(1)) register_4 (.D(overflow_t), .clk(buffer_1_out), .Q(Overflow));  // open: en, clr

  assign \end  = start;

  // Other names for the same wires on the sheet: EA[7:0] = A[30:23]; SA = A[31]; EB[7:0] = B[30:23]; SB = B[31];
  //   E_large[7:0] = out_7; FA[22:0] = A[22:0]; MA[22:0] = A[22:0]; MAoMB[23:1] = M1; FB[22:0] = B[22:0];
  //   MB[22:0] = B[22:0]
endmodule
