// Logisim project bcd_to_binary.circ as structural Verilog: 2 circuits, main circuit main
module converter (
  input  [11:0] A,
  input  Start,
  input  clk,
  output [9:0] B,
  output End
);

  wire Cq0, Cq1, Cq2, Cq3, D0b0, D0b1, D0b2, D0b3, D0m0, D0m1, D0m2, D0m3, D0n0, D0n1, D0n2, D0n3, D1b0,
       D1b1, D1b2, D1b3, D1m0, D1m1, D1m2, D1m3, D1n0, D1n1, D1n2, D1n3, D2b0, D2b1, D2b2, D2b3, D2m0, D2m1,
       D2m2, D2m3, D2n0, D2n1, D2n2, D2n3, GND, LD, nCLR, RUN, VCC;

  _74194 U1 (
    .pin1(VCC), .pin2(GND), .pin3(D2m3), .pin4(D2m2), .pin5(D2m1), .pin6(D2m0), .pin7(GND), .pin15(D2b3),
    .pin14(D2b2), .pin13(D2b1), .pin12(D2b0), .pin11(clk), .pin10(LD), .pin9(LD));
  _74194 U2 (
    .pin1(VCC), .pin2(GND), .pin3(D1m3), .pin4(D1m2), .pin5(D1m1), .pin6(D1m0), .pin7(GND), .pin15(D1b3),
    .pin14(D1b2), .pin13(D1b1), .pin12(D1b0), .pin11(clk), .pin10(LD), .pin9(LD));
  _74194 U3 (
    .pin1(VCC), .pin2(GND), .pin3(D0m3), .pin4(D0m2), .pin5(D0m1), .pin6(D0m0), .pin7(GND), .pin15(D0b3),
    .pin14(D0b2), .pin13(D0b1), .pin12(D0b0), .pin11(clk), .pin10(LD), .pin9(LD));
  _7404 U14 (
    .pin1(Start), .pin2(nCLR), .pin3(End), .pin4(RUN), .pin5(GND), .pin13(GND), .pin11(GND), .pin9(GND));  // open: pin6, pin12, pin10, pin8
  _74283 U4 (
    .pin1(D2n1), .pin2(GND), .pin3(D2b2), .pin4(D2n0), .pin5(D2b1), .pin6(GND), .pin7(GND), .pin15(GND),
    .pin14(D2b3), .pin13(D2n2), .pin12(GND), .pin11(GND), .pin10(D2n3));  // open: pin9
  _74283 U5 (
    .pin1(D1n1), .pin2(GND), .pin3(D1b2), .pin4(D1n0), .pin5(D1b1), .pin6(D2b0), .pin7(GND), .pin15(D2b0),
    .pin14(D1b3), .pin13(D1n2), .pin12(D2b0), .pin11(D2b0), .pin10(D1n3));  // open: pin9
  _74283 U6 (
    .pin1(D0n1), .pin2(GND), .pin3(D0b2), .pin4(D0n0), .pin5(D0b1), .pin6(D1b0), .pin7(GND), .pin15(D1b0),
    .pin14(D0b3), .pin13(D0n2), .pin12(D1b0), .pin11(D1b0), .pin10(D0n3));  // open: pin9
  _74161 U13 (
    .pin1(nCLR), .pin2(clk), .pin3(GND), .pin4(GND), .pin5(GND), .pin6(GND), .pin7(RUN), .pin14(Cq0),
    .pin13(Cq1), .pin12(Cq2), .pin11(Cq3), .pin10(RUN), .pin9(VCC));  // open: pin15
  _74157 U7 (
    .pin1(Start), .pin2(D2n0), .pin3(A[8]), .pin4(D2m0), .pin5(D2n1), .pin6(A[9]), .pin7(D2m1), .pin15(GND),
    .pin14(D2n3), .pin13(A[11]), .pin12(D2m3), .pin11(D2n2), .pin10(A[10]), .pin9(D2m2));
  _74157 U8 (
    .pin1(Start), .pin2(D1n0), .pin3(A[4]), .pin4(D1m0), .pin5(D1n1), .pin6(A[5]), .pin7(D1m1), .pin15(GND),
    .pin14(D1n3), .pin13(A[7]), .pin12(D1m3), .pin11(D1n2), .pin10(A[6]), .pin9(D1m2));
  _74157 U9 (
    .pin1(Start), .pin2(D0n0), .pin3(A[0]), .pin4(D0m0), .pin5(D0n1), .pin6(A[1]), .pin7(D0m1), .pin15(GND),
    .pin14(D0n3), .pin13(A[3]), .pin12(D0m3), .pin11(D0n2), .pin10(A[2]), .pin9(D0m2));
  _7408 U15 (
    .pin1(Cq1), .pin2(Cq3), .pin3(End), .pin4(GND), .pin5(GND), .pin13(GND), .pin12(GND), .pin10(GND),
    .pin9(GND));  // open: pin6, pin11, pin8
  _74194 U10 (
    .pin1(nCLR), .pin2(D0b0), .pin3(GND), .pin4(GND), .pin5(GND), .pin6(GND), .pin7(GND), .pin15(B[9]),
    .pin14(B[8]), .pin13(B[7]), .pin12(B[6]), .pin11(clk), .pin10(GND), .pin9(RUN));
  _74194 U11 (
    .pin1(nCLR), .pin2(B[6]), .pin3(GND), .pin4(GND), .pin5(GND), .pin6(GND), .pin7(GND), .pin15(B[5]),
    .pin14(B[4]), .pin13(B[3]), .pin12(B[2]), .pin11(clk), .pin10(GND), .pin9(RUN));
  _74194 U12 (
    .pin1(nCLR), .pin2(B[2]), .pin3(GND), .pin4(GND), .pin5(GND), .pin6(GND), .pin7(GND), .pin15(B[1]),
    .pin14(B[0]), .pin11(clk), .pin10(GND), .pin9(RUN));  // open: pin13, pin12
  _7432 U16 (
    .pin1(Start), .pin2(RUN), .pin3(LD), .pin4(GND), .pin5(GND), .pin13(GND), .pin12(GND), .pin10(GND),
    .pin9(GND));  // open: pin6, pin11, pin8
  // also tied to GND on the sheet: GND
  // also tied to VCC on the sheet: VCC

  // Other names for the same wires on the sheet: D0i0 = A[0]; D0i1 = A[1]; D0i2 = A[2]; D0i3 = A[3]; D1i0 = A[4];
  //   D1i1 = A[5]; D1i2 = A[6]; D1i3 = A[7]; D2i0 = A[8]; D2i1 = A[9]; D2i2 = A[10]; D2i3 = A[11]; ST = Start

  // Notes on the sheet:
  //   INPUTS
  //   A = 3-digit BCD, 12 bits: A[11:8]=hundreds A[7:4]=tens A[3:0]=units
  //   U1  74194  D2 digit register
  //   U2  74194  D1 digit register
  //   U3  74194  D0 digit register
  //   U14  7404  nCLR = !Start,  RUN = !End
  //   U4  74283  D2: shift right, -3 if MSB
  //   U5  74283  D1: shift right, -3 if MSB
  //   U6  74283  D0: shift right, -3 if MSB
  //   U13  74161  iteration counter, stops at 10
  //   U7  74157  D2: Start ? A : corrected
  //   U8  74157  D1: Start ? A : corrected
  //   U9  74157  D0: Start ? A : corrected
  //   U15  7408  End = Cq3 . Cq1  (count = 10)
  //   U10  74194  binary result B9..B6
  //   U11  74194  binary result B5..B2
  //   U12  74194  binary result B1..B0
  //   U16  7432  LD = Start + RUN
  //   OUTPUTS
endmodule

module main (
  input  [3:0] A2,
  input  [3:0] A1,
  input  [3:0] A0,
  input  Start,
  output [9:0] B,
  output End
);

  wire CLK_out;

  Clock CLK (.out(CLK_out));
  Hex_Digit_Display hex_digit_display_1 (.value(A2));  // open: dp
  Hex_Digit_Display hex_digit_display_2 (.value(A1));  // open: dp
  Hex_Digit_Display hex_digit_display_3 (.value(A0), .dp(A0[0]));
  converter converter_1 (.A({A2, A1, A0}), .Start(Start), .clk(CLK_out), .B(B), .End(End));
  // Pins of 1 and 4 bits meet at A0

  // Notes on the sheet:
  //   BCD INPUT
  //   hundreds
  //   tens
  //   3-digit BCD to 10-bit binary converter  (74-series TTL)
  //   Start = 1 for one clock to load, then Start = 0; after 10 clocks End = 1 and B is valid.
  //   units
  //   BINARY RESULT (hex)
  //   B[9:8] B[7:4] B[3:0]  -- most significant on the left
endmodule
