// Logisim project alu_regfile.circ as structural Verilog: 2 circuits, main circuit main
module datapath (
  input  [5:0] IR,
  input  clk,
  input  WE,
  input  rst,
  output [7:0] R0,
  output [7:0] R1,
  output [7:0] R2,
  output [7:0] R3,
  output [7:0] ALUout,
  output Cout
);

  wire EN0, EN1, EN2, EN3, nD0, nD1;
  wire [7:0] BX, SRCV;

  xor xor_1 (BX[0], SRCV[0], IR[5]);
  xor xor_2 (BX[1], SRCV[1], IR[5]);
  xor xor_3 (BX[2], SRCV[2], IR[5]);
  xor xor_4 (BX[3], SRCV[3], IR[5]);
  xor xor_5 (BX[4], SRCV[4], IR[5]);
  xor xor_6 (BX[5], SRCV[5], IR[5]);
  xor xor_7 (BX[6], SRCV[6], IR[5]);
  xor xor_8 (BX[7], SRCV[7], IR[5]);
  Multiplexer #(.select(3), .width(8)) multiplexer_1 (
    .in0(R0), .in1(R1), .in2(R2), .in3(R3), .in4({8{1'b0}}), .in5(8'h1), .in6({8{1'b1}}), .in7({8{1'b0}}),
    .out(SRCV), .sel(IR[2:0]));
  Adder adder_1 (.a(R0), .b(BX), .out(ALUout), .cin(IR[5]), .cout(Cout));
  xor xor_9 (nD0, IR[3], 1'b1);
  xor xor_10 (nD1, IR[4], 1'b1);
  and and_1 (EN0, WE, nD1, nD0);
  and and_2 (EN1, WE, nD1, IR[3]);
  and and_3 (EN2, WE, IR[4], nD0);
  and and_4 (EN3, WE, IR[4], IR[3]);
  Register register_1 (.D(ALUout), .en(EN0), .clk(clk), .Q(R0), .clr(rst));
  Register register_2 (.D(ALUout), .en(EN1), .clk(clk), .Q(R1), .clr(rst));
  Register register_3 (.D(ALUout), .en(EN2), .clk(clk), .Q(R2), .clr(rst));
  Register register_4 (.D(ALUout), .en(EN3), .clk(clk), .Q(R3), .clr(rst));

  // Other names for the same wires on the sheet: SRC[2:0] = IR[2:0]; D0 = IR[3]; DST[1:0] = IR[4:3]; D1 = IR[4];
  //   F = IR[5]; R0Q[7:0] = R0; R1Q[7:0] = R1; R2Q[7:0] = R2; R3Q[7:0] = R3; RES[7:0] = ALUout

  // Notes on the sheet:
  //   INSTRUCTION
  //   write enable: 1 = execute the instruction
  //   IR[5] = F (0 add, 1 sub)   IR[4:3] = destination   IR[2:0] = source
  //   constant -1 (two's complement 0xFF)
  //   SOURCE SELECT
  //   ALU  (add / subtract)
  //   subtract = add the one's complement with carry-in 1
  //   input 7 is reserved (tied to 0)
  //   DESTINATION DECODE
  //   REGISTER FILE
  //   R0  (8 bits)
  //   R1  (8 bits)
  //   R2  (8 bits)
  //   R3  (8 bits)
  //   OUTPUTS
endmodule

module main (
  input  [2:0] SRC,
  input  [1:0] DST,
  input  F,
  input  WE,
  input  rst,
  output [7:0] R0,
  output [7:0] R1,
  output [7:0] R2,
  output [7:0] R3,
  output [7:0] ALUout,
  output Cout
);

  wire CLK_out;

  Clock CLK (.out(CLK_out));
  datapath datapath_1 (
    .IR({F, DST, SRC}), .clk(CLK_out), .WE(WE), .rst(rst), .R3(R3), .ALUout(ALUout), .Cout(Cout), .R0(R0),
    .R1(R1), .R2(R2));

  // Notes on the sheet:
  //   instruction
  //   Arithmetic unit with selectable source and destination
  //   set F / DST / SRC, raise WE, then one clock edge executes the instruction
endmodule
